# Fritzing sketch ASD1115-schematics (saved by Fritzing 0.9.3b)

parts:
  Raspberry_Pi_1 = Raspberry Pi 3 [part_number=RPI-3-V1.2]
  ADS1115 = Adafruit ADS1115 16Bit I2C ADC
  R1 = Rotary Potentiometer (Small) [maximum_resistance=10kΩ package=THT]

nets:
  3V3: Raspberry_Pi_1.3v3, Raspberry_Pi_1.3V3, ADS1115.VDD, R1.leg1
  N1: Raspberry_Pi_1.GPIO2, ADS1115.SDA
  N2: Raspberry_Pi_1.GPIO3, ADS1115.SCL
  GND: Raspberry_Pi_1.GND, ADS1115.GND, R1.leg2
  N3: ADS1115.AIN0, R1.wiper

custom parts:
  Adafruit ADS1115 16Bit I2C ADC: For microcontrollers without an analog-to-digital converter or when you want a higher-precision ADC, the ADS1115 provides 16-bit precision at 860 samples/second over I2C. The chip can be configured as 4 single-ended input channels, or two differential channels. As a nice bonus, it even includes a programmable gain amplifier, up to x16, to help boost up smaller single/differential signals to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
